# Fritzing sketch carecompanion (saved by Fritzing 0.8.7b)

parts:
  M1 = MakerFocus MAX30102
  M2 = DOIT Esp32 DevKit v1 (30 pins long, 11 pins width) [part_number=ESP32S-PIN30]
  GY1 = MPU-6050 Board GY-521 [form="♀ (female)" package=THT]
  A1 = HuskyLens-Vision-Sensor_1
  OLED_I2C1 = OLED 128x64 I2C Monochrome Display
  J1 = Piezo Speaker  # not connected
  TP1 = TP4056 [chip_label=TP4056 package="DIP (Dual Inline) [THT]"]
  U2 = LIPO-2000mAh [package=lipo-2000]
  S1 = Round Pushbutton
  M3 = bn-220- GPS-module
  M4 = sim800L v2 evb

nets:
  GND: M1.GND, M2.GND, M2.D35, M2.D32, GY1.pin2, A1.pin3, OLED_I2C1.GND, TP1.pin6, S1.leg0, M3.pin_1, M4.pin_2, M4.pin_6
  N1: M1.SCL, M2.TX0, M2.D22, GY1.pin3, A1.pin2, OLED_I2C1.SCK
  N2: M1.SDA, M2.D21, GY1.pin4, A1.pin1, OLED_I2C1.SDA
  VIN: M1.VIN, M2.3V3, GY1.pin1, A1.pin4, OLED_I2C1.VDD
  N3: M2.RX2, M3.pin_2
  N4: M2.TX2, M3.pin_3
  N5: M2.D25, M4.pin_3
  N6: M2.D26, M4.pin_4
  N7: M2.D13, S1.leg1
  N8: M2.VIN, TP1.pin3, M3.pin_4, M4.pin_5
  N9: TP1.pin4, U2.+
  N10: TP1.pin5, U2.-

custom parts:
  MakerFocus MAX30102: Oximeter module using the MAX30102 chip. As usual, if you want the mounting holes in pcb, you need to drag a hole over the pad in silkscreen to actually drill the hole (by default they are not drilled)
  DOIT Esp32 DevKit v1 (30 pins long, 11 pins width): The DOIT Esp32 DevKit v1 is one of the development board created by DOIT to evaluate the ESP-WROOM-32 module. It is based on the ESP32 microcontroller that boasts Wifi, Bluetooth, Ethernet and Low Power support all in a single chip. (vanepp) made breadboard work, adjusted pin numbering and labels and reduced size of schematic and cleaned up pcb. This chip is 30pins long (2 x15) and 11 pins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
  MPU-6050 Board GY-521: Acelerometro y Giroscopio MPU-6050 Board GY-521
  HuskyLens-Vision-Sensor_1: Huskylens is an easy-to-use AI Camera | Vision Sensor. DFrobot Huskylens is equipped with multiple functions, such as face recognition, object tracking, object recognition, line tracking, color recognition, and tag(QR code) recognition.
  TP4056: A DIP stand-in part for whatever IC you want. With 6 pins on a 300mil dual inline package (DIP) footprint.
  bn-220- GPS-module: bn-220l GPS module. Chipset : 8030-KT Receiving Format : GPS,GLONASS,Galileo,BeiDou,QZSS and SBAS
  sim800L v2 evb: sim800L v2 evb GSM module.
